# Fritzing sketch tally-schematics (saved by Fritzing 0.9.2b)
breadboards: 1

parts:
  U1 = NodeMCU V3.0
  RGB_Strip_LED1 = RGB Strip LED

nets:
  N1: U1.3V3, RGB_Strip_LED1.Common_Connect
  N2: U1.GND#6, U1.GND#13, U1.GND#16, U1.GND#33
  N3: U1.D5, RGB_Strip_LED1.Blue_Connect
  N4: U1.D6, RGB_Strip_LED1.Red_Connect
  N5: U1.D7, RGB_Strip_LED1.Green_Connect

custom parts:
  NodeMCU V3.0: ESP8266 based NodeMCU
  RGB Strip LED: A tri-color Strip LED with red, green and blue. Based on LED SMD 5050 RGB Pin order: common cathode - green - red - blue
